// Logisim project ARS1.circ as structural Verilog: 1 circuit, main circuit main
module main (
  input  A3,
  input  A2,
  input  A1,
  input  A0,
  input  B3,
  input  B2,
  input  B1,
  input  B0,
  output out_9,
  output out_10,
  output out_11,
  output out_12,
  output out_13,
  output out_14,
  output out_15,
  output out_16
);

  wire [1:0] or_1_out;

  Multiplexer #(.select(2), .enable("false")) multiplexer_1 (
    .in0(A3), .in1(A3), .in2(A3), .in3(A3), .out(out_9), .sel(or_1_out));
  Multiplexer #(.select(2), .enable("false")) multiplexer_2 (
    .in0(A2), .in1(A3), .in2(A3), .in3(A3), .out(out_14), .sel(or_1_out));
  Multiplexer #(.select(2), .enable("false")) multiplexer_3 (
    .in0(A1), .in1(A2), .in2(A3), .in3(A3), .out(out_15), .sel(or_1_out));
  Multiplexer #(.select(2), .enable("false")) multiplexer_4 (
    .in0(A0), .in1(A1), .in2(A2), .in3(A3), .out(out_16), .sel(or_1_out));
  or or_1 (or_1_out[0], B0, B2, B3);
  or or_2 (or_1_out[1], B1, B2, B3);

  assign out_10 = out_9;
  assign out_11 = out_9;
  assign out_12 = out_9;
  assign out_13 = out_9;
endmodule
