// Logisim project AddSub.circ as structural Verilog
module Adder (
  input  in_1,
  input  in_2,
  input  in_3,
  output out_4,
  output out_5
);

  wire and_1_out, and_2_out, xor_1_out;

  xor xor_1 (xor_1_out, in_1, in_2);
  xor xor_2 (out_4, xor_1_out, in_3);
  and and_1 (and_1_out, in_3, xor_1_out);
  and and_2 (and_2_out, in_1, in_2);
  or or_1 (out_5, and_1_out, and_2_out);
endmodule

module Add_Sub (
  input  Cin,
  input  B0,
  input  B1,
  input  B2,
  input  Signed_Bit,
  input  A0,
  input  A1,
  input  A2,
  input  Signed_Bit_2,
  output Sum0,
  output Sum1,
  output Sum2,
  output Sum3,
  output Sum4,
  output Sum5,
  output Sum6,
  output Sum7
);

  wire adder_1_out_5, adder_2_out_5, adder_3_out_5, adder_4_out_5, adder_5_out_5, adder_6_out_5,
       adder_7_out_5, xor_1_out, xor_2_out, xor_3_out, xor_4_out, xor_5_out, xor_6_out, xor_7_out, xor_8_out;

  xor xor_1 (xor_1_out, Cin, B0);
  Adder adder_1 (.in_1(A0), .in_2(xor_1_out), .in_3(Cin), .out_4(Sum0), .out_5(adder_1_out_5));
  xor xor_2 (xor_2_out, Cin, B1);
  Adder adder_2 (.in_1(A1), .in_2(xor_2_out), .in_3(adder_1_out_5), .out_4(Sum1), .out_5(adder_2_out_5));
  xor xor_3 (xor_3_out, Cin, B2);
  xor xor_4 (xor_4_out, Cin, Signed_Bit);
  Adder adder_3 (.in_1(A2), .in_2(xor_3_out), .in_3(adder_2_out_5), .out_4(Sum2), .out_5(adder_3_out_5));
  Adder adder_4 (.in_1(Signed_Bit_2), .in_2(xor_4_out), .in_3(adder_3_out_5), .out_4(Sum3), .out_5(adder_4_out_5));
  xor xor_5 (xor_5_out, Cin, Signed_Bit);
  Adder adder_5 (.in_1(Signed_Bit_2), .in_2(xor_5_out), .in_3(adder_4_out_5), .out_4(Sum4), .out_5(adder_5_out_5));
  xor xor_6 (xor_6_out, Cin, Signed_Bit);
  xor xor_7 (xor_7_out, Cin, Signed_Bit);
  Adder adder_6 (.in_1(Signed_Bit_2), .in_2(xor_6_out), .in_3(adder_5_out_5), .out_4(Sum5), .out_5(adder_6_out_5));
  Adder adder_7 (.in_1(Signed_Bit_2), .in_2(xor_7_out), .in_3(adder_6_out_5), .out_4(Sum6), .out_5(adder_7_out_5));
  xor xor_8 (xor_8_out, Cin, Signed_Bit);
  Adder adder_8 (.in_1(Signed_Bit_2), .in_2(xor_8_out), .in_3(adder_7_out_5), .out_4(Sum7));  // open: out_5
endmodule
