// Logisim project block1.circ as structural Verilog: 3 circuits, main circuit main
module main (
  input  cin,
  input  A,
  input  B,
  input  N,
  output D,
  output R,
  output Cout
);

  Adder #(.width(1)) adder_1 (.a(A), .b(B), .out(D), .cin(cin), .cout(Cout));
  Multiplexer #(.enable("false")) multiplexer_1 (.in0(D), .in1(A), .out(R), .sel(N));
endmodule

module Mod (
  input  B3,
  input  B2,
  input  B1,
  input  B0,
  input  A3,
  input  A2,
  input  A1,
  input  A0,
  output R3,
  output R2,
  output R1,
  output R0
);

  wire main_1_d, main_2_d, main_3_d, main_4_d, main_5_cout, main_5_r, main_6_cout, main_6_r, main_7_cout,
       main_7_r, main_8_cout, main_9_cout, main_9_r, main_10_cout, main_10_r, main_11_cout, main_11_r,
       main_12_cout, main_13_cout, main_13_r, main_14_cout, main_14_r, main_15_cout, main_15_r, main_16_cout,
       not_1_out, not_2_out, not_3_out, not_4_out, not_5_out, not_6_out, not_7_out, not_8_out, not_9_out,
       not_10_out, not_11_out, not_12_out, not_13_out, not_14_out, not_15_out, not_16_out;

  not not_1 (not_1_out, B3);
  main main_1 (.B(not_1_out), .A(1'b0), .N(main_1_d), .cin(main_5_cout), .D(main_1_d));  // open: R, Cout
  not not_2 (not_2_out, B3);
  main main_2 (.B(not_2_out), .A(main_5_r), .N(main_2_d), .cin(main_6_cout), .D(main_2_d));  // open: R, Cout
  not not_3 (not_3_out, B3);
  main main_3 (.B(not_3_out), .A(main_6_r), .N(main_3_d), .cin(main_7_cout), .D(main_3_d));  // open: R, Cout
  not not_4 (not_4_out, B3);
  main main_4 (.B(not_4_out), .A(main_7_r), .N(main_4_d), .cin(main_8_cout), .D(main_4_d), .R(R3));  // open: Cout
  not not_5 (not_5_out, B2);
  not not_6 (not_6_out, B2);
  not not_7 (not_7_out, B2);
  not not_8 (not_8_out, B2);
  main main_5 (.B(not_5_out), .A(1'b0), .N(main_1_d), .cin(main_9_cout), .R(main_5_r), .Cout(main_5_cout));  // open: D
  main main_6 (
    .B(not_6_out), .A(main_9_r), .N(main_2_d), .cin(main_10_cout), .R(main_6_r), .Cout(main_6_cout));  // open: D
  main main_7 (
    .B(not_7_out), .A(main_10_r), .N(main_3_d), .cin(main_11_cout), .R(main_7_r), .Cout(main_7_cout));  // open: D
  main main_8 (.B(not_8_out), .A(main_11_r), .N(main_4_d), .cin(main_12_cout), .R(R2), .Cout(main_8_cout));  // open: D
  not not_9 (not_9_out, B1);
  main main_9 (.B(not_9_out), .A(1'b0), .N(main_1_d), .cin(main_13_cout), .R(main_9_r), .Cout(main_9_cout));  // open: D
  not not_10 (not_10_out, B1);
  main main_10 (
    .B(not_10_out), .A(main_13_r), .N(main_2_d), .cin(main_14_cout), .R(main_10_r), .Cout(main_10_cout));  // open: D
  not not_11 (not_11_out, B1);
  main main_11 (
    .B(not_11_out), .A(main_14_r), .N(main_3_d), .cin(main_15_cout), .R(main_11_r), .Cout(main_11_cout));  // open: D
  not not_12 (not_12_out, B1);
  main main_12 (
    .B(not_12_out), .A(main_15_r), .N(main_4_d), .cin(main_16_cout), .R(R1), .Cout(main_12_cout));  // open: D
  not not_13 (not_13_out, B0);
  main main_13 (.B(not_13_out), .A(A3), .N(main_1_d), .cin(1'b1), .R(main_13_r), .Cout(main_13_cout));  // open: D
  not not_14 (not_14_out, B0);
  main main_14 (.B(not_14_out), .A(A2), .N(main_2_d), .cin(1'b1), .R(main_14_r), .Cout(main_14_cout));  // open: D
  not not_15 (not_15_out, B0);
  main main_15 (.B(not_15_out), .A(A1), .N(main_3_d), .cin(1'b1), .R(main_15_r), .Cout(main_15_cout));  // open: D
  not not_16 (not_16_out, B0);
  main main_16 (.B(not_16_out), .A(A0), .N(main_4_d), .cin(1'b1), .R(R0), .Cout(main_16_cout));  // open: D
endmodule

module mod_f (
  input  in_1,
  input  in_2,
  input  in_3,
  input  in_4,
  input  in_5,
  input  in_6,
  input  in_7,
  input  in_8,
  input  [3:0] in_9,
  input  [3:0] in_10,
  output out_11,
  output out_12,
  output out_13,
  output out_14
);

  wire [3:0] adder_1_out, adder_2_out, not_1_out, not_5_out;

  not not_1 (not_1_out[0], in_4);
  not not_2 (not_1_out[1], in_3);
  not not_3 (not_1_out[2], in_2);
  not not_4 (not_1_out[3], in_1);
  Adder #(.width(4)) adder_1 (.a(not_1_out), .b(in_9), .out(adder_1_out), .cin(1'b0));  // open: cout
  Mod mod_1 (
    .B3(adder_1_out[3]), .B2(adder_1_out[2]), .B1(adder_1_out[1]), .B0(adder_1_out[0]), .A3(adder_2_out[3]),
    .A2(adder_2_out[2]), .A1(adder_2_out[1]), .A0(adder_2_out[0]), .R3(out_11), .R2(out_12), .R1(out_13),
    .R0(out_14));
  not not_5 (not_5_out[0], in_8);
  not not_6 (not_5_out[1], in_7);
  not not_7 (not_5_out[2], in_6);
  not not_8 (not_5_out[3], in_5);
  Adder #(.width(4)) adder_2 (.a(not_5_out), .b(in_10), .out(adder_2_out), .cin(1'b0));  // open: cout
endmodule
