// Logisim project mult.circ as structural Verilog: 1 circuit, main circuit main
module main (
  input  A3,
  input  A2,
  input  A1,
  input  A0,
  input  B0,
  input  B1,
  input  B2,
  input  B3,
  output O0,
  output O1,
  output O2,
  output O3,
  output O4,
  output O5,
  output O6,
  output O7
);

  wire adder_2_cout, adder_2_out, adder_3_cout, adder_4_cout, adder_4_out, adder_5_cout, adder_5_out,
       adder_6_cout, adder_6_out, adder_7_cout, adder_8_cout, adder_8_out, adder_9_cout, adder_9_out,
       adder_10_cout, adder_11_cout, adder_12_cout, adder_13_cout, and_1_out, and_2_out, and_3_out,
       and_4_out, and_5_out, and_6_out, and_7_out, and_9_out, and_10_out, nand_1_out, nand_2_out, nand_3_out,
       nand_4_out, nand_5_out, nand_6_out;

  Adder #(.width(1)) adder_1 (.a(adder_3_cout), .b(1'b1), .out(O7), .cin(1'b0));  // open: cout
  nand nand_1 (nand_1_out, A3, B1);
  nand nand_2 (nand_2_out, A3, B2);
  Adder #(.width(1)) adder_2 (
    .a(nand_2_out), .b(adder_4_cout), .out(adder_2_out), .cin(adder_6_cout), .cout(adder_2_cout));
  and and_1 (and_1_out, A3, B3);
  Adder #(.width(1)) adder_3 (.a(and_1_out), .b(adder_2_cout), .out(O6), .cin(adder_7_cout), .cout(adder_3_cout));
  nand nand_3 (nand_3_out, A3, B0);
  Adder #(.width(1)) adder_4 (.a(nand_1_out), .b(1'b1), .out(adder_4_out), .cin(adder_5_cout), .cout(adder_4_cout));
  and and_2 (and_2_out, A2, B2);
  nand nand_4 (nand_4_out, A2, B3);
  and and_3 (and_3_out, A2, B0);
  and and_4 (and_4_out, A2, B1);
  Adder #(.width(1)) adder_5 (
    .a(and_4_out), .b(nand_3_out), .out(adder_5_out), .cin(adder_8_cout), .cout(adder_5_cout));
  Adder #(.width(1)) adder_6 (
    .a(and_2_out), .b(adder_4_out), .out(adder_6_out), .cin(adder_9_cout), .cout(adder_6_cout));
  Adder #(.width(1)) adder_7 (.a(nand_4_out), .b(adder_2_out), .out(O5), .cin(adder_10_cout), .cout(adder_7_cout));
  and and_5 (and_5_out, A1, B1);
  Adder #(.width(1)) adder_8 (
    .a(and_5_out), .b(and_3_out), .out(adder_8_out), .cin(adder_13_cout), .cout(adder_8_cout));
  and and_6 (and_6_out, A1, B2);
  Adder #(.width(1)) adder_9 (
    .a(and_6_out), .b(adder_5_out), .out(adder_9_out), .cin(adder_11_cout), .cout(adder_9_cout));
  nand nand_5 (nand_5_out, A1, B3);
  Adder #(.width(1)) adder_10 (.a(nand_5_out), .b(adder_6_out), .out(O4), .cin(adder_12_cout), .cout(adder_10_cout));
  and and_7 (and_7_out, A1, B0);
  nand nand_6 (nand_6_out, A0, B3);
  and and_8 (O0, A0, B0);
  and and_9 (and_9_out, A0, B1);
  and and_10 (and_10_out, A0, B2);
  Adder #(.width(1)) adder_11 (.a(and_10_out), .b(adder_8_out), .out(O2), .cin(1'b0), .cout(adder_11_cout));
  Adder #(.width(1)) adder_12 (.a(nand_6_out), .b(adder_9_out), .out(O3), .cin(1'b0), .cout(adder_12_cout));
  Adder #(.width(1)) adder_13 (.a(and_9_out), .b(and_7_out), .out(O1), .cin(1'b0), .cout(adder_13_cout));
  // AND_Gate and_11 is placed but not wired
  // AND_Gate and_12 is placed but not wired
  // AND_Gate and_13 is placed but not wired
  Adder #(.width(1)) adder_14 ();  // open: a, b, out, cin, cout
  // AND_Gate and_14 is placed but not wired

  // Notes on the sheet:
  //   B1: pull=up
endmodule
